# Fritzing sketch sketch (saved by Fritzing 0.9.9b)
circuit board: 13cm x 7.4cm
breadboards: 2

parts:
  Součástka1 = MAX3232
  A1 = ESP32 DevKitc V4
  IC1 = ULN2803A [package=THT]
  IC2 = ULN2803A [package=THT]
  IC3 = ULN2803A [package=THT]
  U1 = LM2596 step down module
  JACK1 = 2.1mm Barrel Jack with Terminal Block
  J1 = female pin header, 48 pins [form="♀ (female)"]

nets:
  N1: Součástka1.VCC, A1.Pin_19, U1.OUT+
  N2: Součástka1.RXD, A1.Pin_34
  N3: Součástka1.TXD, A1.Pin_35
  N4: Součástka1.GND, A1.Pin_14, A1.Pin_32, A1.Pin_38, IC1.0V, IC2.0V, IC3.0V, U1.IN-, U1.OUT-, JACK1.NEG, J1.pin2, J1.pin4, J1.pin6, J1.pin8, J1.pin10, J1.pin12, J1.pin14, J1.pin16, J1.pin18, J1.pin20, J1.pin22, J1.pin24, J1.pin26, J1.pin28, J1.pin30, J1.pin32, J1.pin34, J1.pin36, J1.pin38, J1.pin40, J1.pin42, J1.pin44, J1.pin46, J1.pin48
  N5: IC1.COM_-_Common, IC2.COM_-_Common, IC3.COM_-_Common, U1.IN+, JACK1.POS
  N6: IC1.Out_8, J1.pin15
  N7: IC1.Out_7, J1.pin13
  N8: IC1.Out_6, J1.pin11
  N9: IC1.Out_5, J1.pin9
  N10: IC1.Out_4, J1.pin7
  N11: IC1.Out_3, J1.pin5
  N12: IC1.Out_2, J1.pin3
  N13: IC1.Out_1, J1.pin1
  N14: IC2.Out_8, J1.pin31
  N15: IC2.Out_7, J1.pin29
  N16: IC2.Out_6, J1.pin27
  N17: IC2.Out_5, J1.pin25
  N18: IC2.Out_4, J1.pin23
  N19: IC2.Out_3, J1.pin21
  N20: IC2.Out_2, J1.pin19
  N21: IC2.Out_1, J1.pin17
  N22: IC3.Out_8, J1.pin47
  N23: IC3.Out_7, J1.pin45
  N24: IC3.Out_6, J1.pin43
  N25: IC3.Out_5, J1.pin41
  N26: IC3.Out_4, J1.pin39
  N27: IC3.Out_3, J1.pin37
  N28: IC3.Out_2, J1.pin35
  N29: IC3.Out_1, J1.pin33

custom parts:
  MAX3232: A random MAX3232 Breakout Board from AliExpress (RS232-TTL-Converter)
  ESP32 DevKitc V4: ESP32-DevKitC board with ESP32-WROOM-32 module. ESP32-DevKitC V4 is a small-sized ESP32-based development board produced by Espressif. Most of the pins on the ESP module are broken out to the pin headers on the board. The pins D0, D1, D2, D3, CMD and CLK are used internally for communication between ESP32 and SPI flash memory. They are grouped on both sides near the USB connector. Avoid using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
  LM2596 step down module: LM2596 DC-DC step down power supply module 3 A.
